// Logisim project control_logic.circ as structural Verilog: 1 circuit, main circuit control_logic
module control_logic (
  input  [31:0] inst,
  input  BrEq,
  input  BrLt,
  output PCSel,
  output RegWEn,
  output [2:0] ImmSel,
  output BrUn,
  output ASel,
  output BSel,
  output [3:0] ALUSel,
  output [3:0] MemRW,
  output [2:0] WBSel,
  output CSRSel,
  output CSRWen,
  output InstFlush
);

  wire and_1_out, and_3_out, and_4_out, and_6_out, and_7_out, and_9_out, and_10_out, and_11_out, and_12_out,
       and_13_out, and_14_out, and_15_out, and_16_out, and_17_out, and_18_out, and_19_out, and_20_out,
       and_21_out, and_22_out, and_23_out, and_24_out, and_25_out, and_26_out, and_27_out, comparator_1_eq,
       comparator_2_eq, comparator_3_eq, comparator_4_eq, comparator_5_eq, comparator_6_eq, comparator_8_eq,
       comparator_9_eq, comparator_10_eq, comparator_12_eq, comparator_13_eq, comparator_14_eq,
       comparator_15_eq, comparator_16_eq, comparator_17_eq, comparator_18_eq, comparator_19_eq,
       comparator_20_eq, comparator_21_eq, comparator_22_eq, comparator_23_eq, comparator_24_eq,
       comparator_25_eq, comparator_26_eq, comparator_27_eq, comparator_28_eq, comparator_29_eq,
       comparator_30_eq, comparator_31_eq, comparator_32_eq, comparator_33_eq, comparator_34_eq,
       comparator_35_eq, not_2_out, not_3_out, not_4_out, or_1_out, or_2_out, or_3_out, or_7_out, R;

  or or_1 (or_1_out, comparator_4_eq, comparator_1_eq);
  not not_1 (RegWEn, or_1_out);
  Comparator #(.width(7)) comparator_1 (.a(7'b1100011), .b(inst[6:0]), .eq(comparator_1_eq));  // open: gt, lt
  Comparator #(.width(7)) comparator_2 (.a(7'b1101111), .b(inst[6:0]), .eq(comparator_2_eq));  // open: gt, lt
  Comparator #(.width(7)) comparator_3 (.a(7'b1100111), .b(inst[6:0]), .eq(comparator_3_eq));  // open: gt, lt
  Comparator #(.width(7)) comparator_4 (.a(7'b0100011), .b(inst[6:0]), .eq(comparator_4_eq));  // open: gt, lt
  Comparator #(.width(7)) comparator_5 (.a(7'b0010111), .b(inst[6:0]), .eq(comparator_5_eq));  // open: gt, lt
  Comparator #(.width(7)) comparator_6 (.a(7'b0110111), .b(inst[6:0]), .eq(comparator_6_eq));  // open: gt, lt
  Comparator #(.width(7)) comparator_7 (.a(7'b0110011), .b(inst[6:0]), .eq(R));  // open: gt, lt
  Comparator #(.width(7)) comparator_8 (.a(7'b0000011), .b(inst[6:0]), .eq(comparator_8_eq));  // open: gt, lt
  Comparator #(.width(7)) comparator_9 (.a(7'b0010011), .b(inst[6:0]), .eq(comparator_9_eq));  // open: gt, lt
  Comparator #(.width(3)) comparator_10 (.a(3'b001), .b(inst[14:12]), .eq(comparator_10_eq));  // open: gt, lt
  Comparator #(.width(7)) comparator_11 (.a(7'b1110011), .b(inst[6:0]), .eq(CSRWen));  // open: gt, lt
  Comparator #(.width(3)) comparator_12 (.a(3'b101), .b(inst[14:12]), .eq(comparator_12_eq));  // open: gt, lt
  and and_1 (and_1_out, comparator_10_eq, CSRWen);
  and and_2 (CSRSel, CSRWen, comparator_12_eq);
  Comparator #(.width(3)) comparator_13 (.a(3'b000), .b(inst[14:12]), .eq(comparator_13_eq));  // open: gt, lt
  Comparator #(.width(3)) comparator_14 (.a(3'b001), .b(inst[14:12]), .eq(comparator_14_eq));  // open: gt, lt
  Comparator #(.width(3)) comparator_15 (.a(3'b010), .b(inst[14:12]), .eq(comparator_15_eq));  // open: gt, lt
  Comparator #(.width(3)) comparator_16 (.a(3'b000), .b(inst[14:12]), .eq(comparator_16_eq));  // open: gt, lt
  Comparator #(.width(3)) comparator_17 (.a(3'b001), .b(inst[14:12]), .eq(comparator_17_eq));  // open: gt, lt
  Comparator #(.width(3)) comparator_18 (.a(3'b010), .b(inst[14:12]), .eq(comparator_18_eq));  // open: gt, lt
  Comparator #(.width(3)) comparator_19 (.a(3'b110), .b(inst[14:12]), .eq(comparator_19_eq));  // open: gt, lt
  Comparator #(.width(3)) comparator_20 (.a(3'b111), .b(inst[14:12]), .eq(comparator_20_eq));  // open: gt, lt
  or or_2 (or_2_out, comparator_5_eq, comparator_2_eq, comparator_1_eq);
  or or_3 (or_3_out, R, and_1_out);
  and and_3 (and_3_out, comparator_8_eq, comparator_16_eq);
  and and_4 (and_4_out, comparator_8_eq, comparator_17_eq);
  and and_5 (WBSel[2], comparator_8_eq, comparator_18_eq);
  and and_6 (and_6_out, comparator_4_eq, comparator_13_eq);
  and and_7 (and_7_out, comparator_4_eq, comparator_14_eq);
  and and_8 (MemRW[3], comparator_4_eq, comparator_15_eq);
  Comparator #(.width(3)) comparator_21 (.a(3'b000), .b(inst[14:12]), .eq(comparator_21_eq));  // open: gt, lt
  Comparator #(.width(3)) comparator_22 (.a(3'b001), .b(inst[14:12]), .eq(comparator_22_eq));  // open: gt, lt
  not not_2 (not_2_out, BrEq);
  Comparator #(.width(3)) comparator_23 (.a(3'b100), .b(inst[14:12]), .eq(comparator_23_eq));  // open: gt, lt
  Comparator #(.width(3)) comparator_24 (.a(3'b101), .b(inst[14:12]), .eq(comparator_24_eq));  // open: gt, lt
  not not_3 (not_3_out, BrLt);
  not not_4 (not_4_out, BrLt);
  not not_5 (ASel, or_2_out);
  not not_6 (BSel, or_3_out);
  or or_4 (WBSel[1], and_3_out, and_4_out);
  and and_9 (and_9_out, comparator_21_eq, comparator_1_eq, BrEq);
  and and_10 (and_10_out, comparator_22_eq, comparator_1_eq, not_2_out);
  and and_11 (and_11_out, comparator_23_eq, comparator_1_eq, BrLt);
  and and_12 (and_12_out, comparator_24_eq, comparator_1_eq, not_3_out);
  and and_13 (and_13_out, comparator_19_eq, comparator_1_eq);
  and and_14 (and_14_out, and_13_out, BrLt);
  and and_15 (and_15_out, comparator_20_eq, comparator_1_eq);
  and and_16 (and_16_out, and_15_out, not_4_out);
  or or_5 (MemRW[1], and_7_out, MemRW[3]);
  or or_6 (MemRW[0], and_6_out, MemRW[1], MemRW[3]);
  or or_7 (or_7_out, comparator_5_eq, comparator_6_eq, comparator_9_eq, R);
  or or_8 (WBSel[0], or_7_out, and_4_out);
  or or_9 (PCSel, and_9_out, and_10_out, and_11_out, and_12_out, and_14_out, and_16_out, comparator_3_eq, comparator_2_eq);
  or or_10 (BrUn, and_13_out, and_15_out);
  or or_11 (ImmSel[2], comparator_2_eq, CSRSel);
  or or_12 (ImmSel[1], comparator_5_eq, comparator_6_eq, comparator_1_eq);
  or or_13 (ImmSel[0], comparator_4_eq, comparator_5_eq, comparator_6_eq, CSRSel);
  Comparator #(.width(3)) comparator_25 (.a(inst[14:12]), .b(3'b000), .eq(comparator_25_eq));  // open: gt, lt
  Comparator #(.width(3)) comparator_26 (.a(inst[14:12]), .b(3'b001), .eq(comparator_26_eq));  // open: gt, lt
  Comparator #(.width(3)) comparator_27 (.a(inst[14:12]), .b(3'b010), .eq(comparator_27_eq));  // open: gt, lt
  Comparator #(.width(3)) comparator_28 (.a(inst[14:12]), .b(3'b011), .eq(comparator_28_eq));  // open: gt, lt
  Comparator #(.width(3)) comparator_29 (.a(inst[14:12]), .b(3'b100), .eq(comparator_29_eq));  // open: gt, lt
  Comparator #(.width(3)) comparator_30 (.a(inst[14:12]), .b(3'b101), .eq(comparator_30_eq));  // open: gt, lt
  Comparator #(.width(3)) comparator_31 (.a(inst[14:12]), .b(3'b110), .eq(comparator_31_eq));  // open: gt, lt
  Comparator #(.width(3)) comparator_32 (.a(inst[14:12]), .b(3'b111), .eq(comparator_32_eq));  // open: gt, lt
  or or_14 (InstFlush, comparator_2_eq, comparator_3_eq, PCSel);
  Comparator #(.width(7)) comparator_33 (.a(inst[31:25]), .b({7{1'b0}}), .eq(comparator_33_eq));  // open: gt, lt
  and and_17 (and_17_out, comparator_33_eq, comparator_26_eq, R);
  and and_18 (and_18_out, comparator_33_eq, comparator_27_eq, R);
  and and_19 (and_19_out, comparator_33_eq, comparator_29_eq, R);
  and and_20 (and_20_out, comparator_33_eq, comparator_30_eq, R);
  and and_21 (and_21_out, comparator_33_eq, comparator_31_eq, R);
  and and_22 (and_22_out, comparator_33_eq, comparator_32_eq, R);
  Comparator #(.width(7)) comparator_34 (.a(inst[31:25]), .b(7'b0000001), .eq(comparator_34_eq));  // open: gt, lt
  and and_23 (and_23_out, comparator_34_eq, comparator_25_eq, R);
  and and_24 (and_24_out, comparator_34_eq, comparator_26_eq, R);
  and and_25 (and_25_out, comparator_34_eq, comparator_28_eq, R);
  Comparator #(.width(7)) comparator_35 (.a(inst[31:25]), .b(7'b0100000), .eq(comparator_35_eq));  // open: gt, lt
  or or_15 (ALUSel[3], and_26_out, and_25_out, comparator_6_eq, and_24_out, and_23_out);
  and and_26 (and_26_out, comparator_35_eq, comparator_25_eq, R);
  and and_27 (and_27_out, comparator_35_eq, comparator_30_eq, R);
  or or_16 (ALUSel[2], and_26_out, and_27_out, and_24_out, comparator_6_eq, and_20_out, and_18_out, and_17_out);
  or or_17 (ALUSel[1], and_20_out, and_24_out, and_17_out, and_23_out, and_25_out, and_19_out, and_21_out);
  or or_18 (ALUSel[0], and_27_out, and_19_out, and_25_out, and_18_out, and_22_out, comparator_6_eq);

  assign MemRW[2] = MemRW[3];

  // Other names for the same wires on the sheet: opcode[6:0] = inst[6:0]; func3[2:0] = inst[14:12];
  //   func7[6:0] = inst[31:25]

  // Notes on the sheet:
  //   INPUTS to your circuit
  //   DON'T CHANGE THE LOCATIONS OF THE INPUTS AND OUTPUTS!
  //   OUTPUT from your circuit
endmodule
