// Logisim project cpu.circ as structural Verilog: 1 circuit, main circuit cpu
module cpu (
  input  clk,
  input  [31:0] INSTRUCTION,
  input  [31:0] READ_DATA,
  output [31:0] WRITE_ADDRESS,
  output [31:0] PROGRAM_COUNTER,
  output [31:0] ra,
  output [31:0] sp,
  output [31:0] t0,
  output [31:0] t1,
  output [31:0] t2,
  output [31:0] s0,
  output [31:0] s1,
  output [31:0] a0,
  output [31:0] tohost,
  output [3:0] WRITE_ENABLE,
  output [31:0] WRITE_DATA
);

  wire branch_comp_1_breq, branch_comp_1_brlt, control_logic_1_asel, control_logic_1_brun,
       control_logic_1_bsel, control_logic_1_csrsel, control_logic_1_csrwen, control_logic_1_instflush,
       control_logic_1_pcsel, control_logic_1_regwen;
  wire [2:0] control_logic_1_immsel, control_logic_1_wbsel;
  wire [3:0] control_logic_1_alusel;
  wire [31:0] adder_1_out, adder_2_out, bit_extender_1_out, bit_extender_2_out, imm_gen_1_imm,
       multiplexer_1_out, multiplexer_2_out, multiplexer_3_out, multiplexer_4_out, multiplexer_5_out,
       multiplexer_6_out, regfile_1_read_data_1, register_1_q, register_2_q;

  Adder #(.width(32)) adder_1 (.a(PROGRAM_COUNTER), .b(32'h4), .out(adder_1_out));  // open: cin, cout
  Multiplexer #(.enable("false"), .width(32)) multiplexer_1 (
    .in0(adder_1_out), .in1(WRITE_ADDRESS), .out(multiplexer_1_out), .sel(control_logic_1_pcsel));
  Register #(.width(32)) PC (.D(multiplexer_1_out), .clk(clk), .Q(PROGRAM_COUNTER));  // open: en, clr
  Multiplexer #(.enable("false"), .width(32)) multiplexer_2 (
    .in0(INSTRUCTION), .in1(32'h13), .out(multiplexer_2_out), .sel(control_logic_1_instflush));
  Register #(.width(32)) register_1 (.D(multiplexer_2_out), .clk(clk), .Q(register_1_q));  // open: en, clr
  control_logic control_logic_1 (
    .CSRWen(control_logic_1_csrwen), .InstFlush(control_logic_1_instflush), .PCSel(control_logic_1_pcsel),
    .RegWEn(control_logic_1_regwen), .ImmSel(control_logic_1_immsel), .BrUn(control_logic_1_brun),
    .ASel(control_logic_1_asel), .BSel(control_logic_1_bsel), .ALUSel(control_logic_1_alusel),
    .MemRW(WRITE_ENABLE), .WBSel(control_logic_1_wbsel), .CSRSel(control_logic_1_csrsel),
    .inst(register_1_q), .BrEq(branch_comp_1_breq), .BrLt(branch_comp_1_brlt));
  Register #(.width(32)) register_2 (.D(PROGRAM_COUNTER), .clk(clk), .Q(register_2_q));  // open: en, clr
  Adder #(.width(32)) adder_2 (.a(register_2_q), .b(32'h4), .out(adder_2_out));  // open: cin, cout
  imm_gen imm_gen_1 (.inst(register_1_q), .ImmSel(control_logic_1_immsel), .imm(imm_gen_1_imm));
  regfile regfile_1 (
    .rs1(register_1_q[19:15]), .rs2(register_1_q[24:20]), .rd(register_1_q[11:7]),
    .Write_Data(multiplexer_6_out), .RegWEn(control_logic_1_regwen), .clk(clk), .ra(ra), .sp(sp), .t0(t0),
    .t1(t1), .t2(t2), .s0(s0), .s1(s1), .a0(a0), .Read_Data_1(regfile_1_read_data_1), .Read_Data_2(WRITE_DATA));
  Multiplexer #(.enable("false"), .width(32)) multiplexer_3 (
    .in0(register_2_q), .in1(regfile_1_read_data_1), .out(multiplexer_3_out), .sel(control_logic_1_asel));
  Multiplexer #(.enable("false"), .width(32)) multiplexer_4 (
    .in0(WRITE_DATA), .in1(imm_gen_1_imm), .out(multiplexer_4_out), .sel(control_logic_1_bsel));
  alu alu_1 (.Result(WRITE_ADDRESS), .A(multiplexer_3_out), .B(multiplexer_4_out), .ALUSel(control_logic_1_alusel));
  branch_comp branch_comp_1 (
    .rs1(regfile_1_read_data_1), .rs2(WRITE_DATA), .BrUn(control_logic_1_brun), .BrEq(branch_comp_1_breq),
    .BrLt(branch_comp_1_brlt));
  Multiplexer #(.enable("false"), .width(32)) multiplexer_5 (
    .in0(regfile_1_read_data_1), .in1(imm_gen_1_imm), .out(multiplexer_5_out), .sel(control_logic_1_csrsel));
  assign bit_extender_1_out = {{24{READ_DATA[7]}}, READ_DATA[7:0]};  // Bit_Extender bit_extender_1
  assign bit_extender_2_out = {{16{READ_DATA[15]}}, READ_DATA[15:0]};  // Bit_Extender bit_extender_2
  csr csr_1 (
    .CSR_address(register_1_q[31:20]), .CSR_din(multiplexer_5_out), .CSR_WE(control_logic_1_csrwen),
    .clk(clk), .tohost(tohost));
  Multiplexer #(.enable("false"), .select(3), .width(32)) multiplexer_6 (
    .in0(adder_2_out), .in1(WRITE_ADDRESS), .in2(bit_extender_1_out), .in3(bit_extender_2_out),
    .in4(READ_DATA), .out(multiplexer_6_out), .sel(control_logic_1_wbsel));  // open: in5, in6, in7

  // Notes on the sheet:
  //   Output to IMEM
  //   IMEM (do **NOT** move this)
  //   Inputs from IMEM
  //   Inputs/Outputs for testing. Do **NOT** move these.
  //   It is OK to move the PC, RegFile, ALU, MEM, Branch Comp, Imm Gen, and Control Logic to wherever is most convenient for you when constructing your CPU, and to delete this text
  //   InstFlush
  //   Outputs To DMEM
  //   DMEM (do **NOT** move this)
  //   Inputs From DMEM
endmodule
