// Logisim project imm_gen.circ as structural Verilog: 1 circuit, main circuit imm_gen
module imm_gen (
  input  [31:0] inst,
  input  [2:0] ImmSel,
  output [31:0] imm
);

  wire [31:0] CSR5;
  wire [31:11] I0, S1;
  wire [31:12] SB2;
  wire [31:20] UJ4;

  Multiplexer #(.enable("false"), .width(21)) multiplexer_1 (
    .in0({21{1'b0}}), .in1({21{1'b1}}), .out(I0), .sel(inst[31]));
  Multiplexer #(.enable("false"), .width(21)) multiplexer_2 (
    .in0({21{1'b0}}), .in1({21{1'b1}}), .out(S1), .sel(inst[31]));
  Multiplexer #(.enable("false"), .width(20)) multiplexer_3 (
    .in0({20{1'b0}}), .in1({20{1'b1}}), .out(SB2), .sel(inst[31]));
  Multiplexer #(.enable("false"), .width(12)) multiplexer_4 (
    .in0({12{1'b0}}), .in1({12{1'b1}}), .out(UJ4), .sel(inst[31]));
  assign CSR5 = {{27{1'b0}}, inst[19:15]};  // Bit_Extender bit_extender_1
  Multiplexer #(.enable("false"), .select(3), .width(32)) multiplexer_5 (
    .in0({I0, inst[30:20]}), .in1({S1, inst[30:25], inst[11:7]}),
    .in2({SB2, inst[7], inst[30:25], inst[11:8], 1'b0}), .in3({inst[31:12], {12{1'b0}}}),
    .in4({UJ4, inst[19:12], inst[20], inst[30:21], 1'b0}), .in5(CSR5), .out(imm), .sel(ImmSel));  // open: in6, in7

  // Other names for the same wires on the sheet: I0[10:0] = inst[30:20]; U3[31:12] = inst[31:12];
  //   UJ4[19:1] = {inst[19:12], inst[20], inst[30:21]}; S1[10:0] = {inst[30:25], inst[11:7]};
  //   SB2[11:1] = {inst[7], inst[30:25], inst[11:8]}

  // Notes on the sheet:
  //   INPUTS to your circuit
  //   DON'T CHANGE THE LOCATIONS OF THE INPUTS AND OUTPUTS!
  //   OUTPUT from your circuit
endmodule
