// Logisim project regfile.circ as structural Verilog: 1 circuit, main circuit regfile
module regfile (
  input  [4:0] rs1,
  input  [4:0] rs2,
  input  [4:0] rd,
  input  [31:0] Write_Data,
  input  RegWEn,
  input  clk,
  output [31:0] ra,
  output [31:0] sp,
  output [31:0] t0,
  output [31:0] t1,
  output [31:0] t2,
  output [31:0] s0,
  output [31:0] s1,
  output [31:0] a0,
  output [31:0] Read_Data_1,
  output [31:0] Read_Data_2
);

  wire demultiplexer_2_out0, x1en, x2en, x3en, x4en, x5en, x6en, x7en, x8en, x9en, x10en, x11en, x12en,
       x13en, x14en, x15en, x16en, x17en, x18en, x19en, x20en, x21en, x22en, x23en, x24en, x25en, x26en,
       x27en, x28en, x29en, x30en, x31en;
  wire [31:0] demultiplexer_1_out0, x1d, x2d, x3d, x3q, x4d, x4q, x5d, x6d, x7d, x8d, x9d, x10d, x11d, x11q,
       x12d, x12q, x13d, x13q, x14d, x14q, x15d, x15q, x16d, x16q, x17d, x17q, x18d, x18q, x19d, x19q, x20d,
       x20q, x21d, x21q, x22d, x22q, x23d, x23q, x24d, x24q, x25d, x25q, x26d, x26q, x27d, x27q, x28d, x28q,
       x29d, x29q, x30d, x30q, x31d, x31q;

  Demultiplexer #(.enable("false"), .select(5), .width(32)) demultiplexer_1 (
    .out0(demultiplexer_1_out0), .out1(x1d), .out2(x2d), .out3(x3d), .out4(x4d), .out5(x5d), .out6(x6d),
    .out7(x7d), .out8(x8d), .out9(x9d), .out10(x10d), .out11(x11d), .out12(x12d), .out13(x13d), .out14(x14d),
    .out15(x15d), .out16(x16d), .out17(x17d), .out18(x18d), .out19(x19d), .out20(x20d), .out21(x21d),
    .out22(x22d), .out23(x23d), .out24(x24d), .out25(x25d), .out26(x26d), .out27(x27d), .out28(x28d),
    .out29(x29d), .out30(x30d), .out31(x31d), .in(Write_Data), .sel(rd));
  Demultiplexer #(.enable("false"), .select(5)) demultiplexer_2 (
    .out0(demultiplexer_2_out0), .out1(x1en), .out2(x2en), .out3(x3en), .out4(x4en), .out5(x5en),
    .out6(x6en), .out7(x7en), .out8(x8en), .out9(x9en), .out10(x10en), .out11(x11en), .out12(x12en),
    .out13(x13en), .out14(x14en), .out15(x15en), .out16(x16en), .out17(x17en), .out18(x18en), .out19(x19en),
    .out20(x20en), .out21(x21en), .out22(x22en), .out23(x23en), .out24(x24en), .out25(x25en), .out26(x26en),
    .out27(x27en), .out28(x28en), .out29(x29en), .out30(x30en), .out31(x31en), .in(RegWEn), .sel(rd));
  Register #(.width(32)) register_1 (.D(x1d), .en(x1en), .clk(clk), .Q(ra));  // open: clr
  Register #(.width(32)) register_2 (.D(x2d), .en(x2en), .clk(clk), .Q(sp));  // open: clr
  Register #(.width(32)) register_3 (.D(x3d), .en(x3en), .clk(clk), .Q(x3q));  // open: clr
  Register #(.width(32)) register_4 (.D(x4d), .en(x4en), .clk(clk), .Q(x4q));  // open: clr
  Register #(.width(32)) register_5 (.D(x17d), .en(x17en), .clk(clk), .Q(x17q));  // open: clr
  Register #(.width(32)) register_6 (.D(x18d), .en(x18en), .clk(clk), .Q(x18q));  // open: clr
  Register #(.width(32)) register_7 (.D(x19d), .en(x19en), .clk(clk), .Q(x19q));  // open: clr
  Register #(.width(32)) register_8 (.D(x20d), .en(x20en), .clk(clk), .Q(x20q));  // open: clr
  Register #(.width(32)) register_9 (.D(x5d), .en(x5en), .clk(clk), .Q(t0));  // open: clr
  Register #(.width(32)) register_10 (.D(x6d), .en(x6en), .clk(clk), .Q(t1));  // open: clr
  Register #(.width(32)) register_11 (.D(x7d), .en(x7en), .clk(clk), .Q(t2));  // open: clr
  Register #(.width(32)) register_12 (.D(x8d), .en(x8en), .clk(clk), .Q(s0));  // open: clr
  Register #(.width(32)) register_13 (.D(x21d), .en(x21en), .clk(clk), .Q(x21q));  // open: clr
  Register #(.width(32)) register_14 (.D(x22d), .en(x22en), .clk(clk), .Q(x22q));  // open: clr
  Register #(.width(32)) register_15 (.D(x23d), .en(x23en), .clk(clk), .Q(x23q));  // open: clr
  Register #(.width(32)) register_16 (.D(x24d), .en(x24en), .clk(clk), .Q(x24q));  // open: clr
  Multiplexer #(.enable("false"), .select(5), .width(32)) multiplexer_1 (
    .in0({32{1'b0}}), .in1(ra), .in2(sp), .in3(x3q), .in4(x4q), .in5(t0), .in6(t1), .in7(t2), .in8(s0),
    .in9(s1), .in10(a0), .in11(x11q), .in12(x12q), .in13(x13q), .in14(x14q), .in15(x15q), .in16(x16q),
    .in17(x17q), .in18(x18q), .in19(x19q), .in20(x20q), .in21(x21q), .in22(x22q), .in23(x23q), .in24(x24q),
    .in25(x25q), .in26(x26q), .in27(x27q), .in28(x28q), .in29(x29q), .in30(x30q), .in31(x31q),
    .out(Read_Data_1), .sel(rs1));
  Register #(.width(32)) register_17 (.D(x9d), .en(x9en), .clk(clk), .Q(s1));  // open: clr
  Register #(.width(32)) register_18 (.D(x10d), .en(x10en), .clk(clk), .Q(a0));  // open: clr
  Register #(.width(32)) register_19 (.D(x11d), .en(x11en), .clk(clk), .Q(x11q));  // open: clr
  Register #(.width(32)) register_20 (.D(x12d), .en(x11en), .clk(clk), .Q(x12q));  // open: clr
  Register #(.width(32)) register_21 (.D(x25d), .en(x25en), .clk(clk), .Q(x25q));  // open: clr
  Register #(.width(32)) register_22 (.D(x26d), .en(x26en), .clk(clk), .Q(x26q));  // open: clr
  Register #(.width(32)) register_23 (.D(x27d), .en(x27en), .clk(clk), .Q(x27q));  // open: clr
  Register #(.width(32)) register_24 (.D(x28d), .en(x28en), .clk(clk), .Q(x28q));  // open: clr
  Multiplexer #(.enable("false"), .select(5), .width(32)) multiplexer_2 (
    .in0({32{1'b0}}), .in1(ra), .in2(sp), .in3(x3q), .in4(x4q), .in5(t0), .in6(t1), .in7(t2), .in8(s0),
    .in9(s1), .in10(a0), .in11(x11q), .in12(x12q), .in13(x13q), .in14(x14q), .in15(x15q), .in16(x16q),
    .in17(x17q), .in18(x18q), .in19(x19q), .in20(x20q), .in21(x21q), .in22(x22q), .in23(x23q), .in24(x24q),
    .in25(x25q), .in26(x26q), .in27(x27q), .in28(x28q), .in29(x29q), .in30(x30q), .in31(x31q),
    .out(Read_Data_2), .sel(rs2));
  Register #(.width(32)) register_25 (.D(x13d), .en(x13en), .clk(clk), .Q(x13q));  // open: clr
  Register #(.width(32)) register_26 (.D(x14d), .en(x14en), .clk(clk), .Q(x14q));  // open: clr
  Register #(.width(32)) register_27 (.D(x15d), .en(x15en), .clk(clk), .Q(x15q));  // open: clr
  Register #(.width(32)) register_28 (.D(x16d), .en(x16en), .clk(clk), .Q(x16q));  // open: clr
  Register #(.width(32)) register_29 (.D(x29d), .en(x29en), .clk(clk), .Q(x29q));  // open: clr
  Register #(.width(32)) register_30 (.D(x30d), .en(x30en), .clk(clk), .Q(x30q));  // open: clr
  Register #(.width(32)) register_31 (.D(x31d), .en(x31en), .clk(clk), .Q(x31q));  // open: clr
  // also tied to GND on the sheet: {demultiplexer_2_out0, demultiplexer_1_out0[0], demultiplexer_1_out0[1], demultiplexer_1_out0[2], demultiplexer_1_out0[3], demultiplexer_1_out0[4], demultiplexer_1_out0[5], demultiplexer_1_out0[6], demultiplexer_1_out0[7], demultiplexer_1_out0[8], demultiplexer_1_out0[9], demultiplexer_1_out0[10], demultiplexer_1_out0[11], demultiplexer_1_out0[12], demultiplexer_1_out0[13], demultiplexer_1_out0[14], demultiplexer_1_out0[15], demultiplexer_1_out0[16], demultiplexer_1_out0[17], demultiplexer_1_out0[18], demultiplexer_1_out0[19], demultiplexer_1_out0[20], demultiplexer_1_out0[21], demultiplexer_1_out0[22], demultiplexer_1_out0[23], demultiplexer_1_out0[24], demultiplexer_1_out0[25], demultiplexer_1_out0[26], demultiplexer_1_out0[27], demultiplexer_1_out0[28], demultiplexer_1_out0[29], demultiplexer_1_out0[30], demultiplexer_1_out0[31]}

  // Other names for the same wires on the sheet: read_reg1[4:0] = rs1; read_reg2[4:0] = rs2;
  //   read_data1[31:0] = Read_Data_1; rs1_t[31:0] = Read_Data_1; read_data2[31:0] = Read_Data_2;
  //   rs2_t[31:0] = Read_Data_2; write_en = RegWEn; write_reg[4:0] = rd; x1q[31:0] = ra; x2q[31:0] = sp;
  //   x5q[31:0] = t0; x6q[31:0] = t1; x7q[31:0] = t2; x8q[31:0] = s0; x9q[31:0] = s1; x10q[31:0] = a0

  // Notes on the sheet:
  //   INPUTS to your circuit
  //   DON'T CHANGE THE LOCATIONS OF THE INPUTS AND OUTPUTS!
  //   These are DEBUG/TEST outputs from your circuit.
  //   OUTPUTS from your circuit
endmodule
